# Fritzing sketch swamy (saved by Fritzing 0.9.6b)
circuit board: 8.64595cm x 6.21431cm
breadboards: 1

parts:
  Mod1 = KY-015 Temperature & Humidity Sensor Module [package="Breakout board"]
  NODEMCU = NodeMCU V1.0
  BUZZER = Piezo Speaker
  Part1 = Arduino Uno (Rev3)
  FlAME_SENSOR = KY-026
  LM393 = FC-28 Soil Hygrometer Module
  part = Header 6 [package=molex-1x6-ra]

nets:
  N1: Mod1.S, NODEMCU.D3
  VIN: Mod1.Vin, BUZZER.pin2, Part1.5V, FlAME_SENSOR.pin3, LM393.VCC, part.6
  GND: Mod1.-, NODEMCU.GND, Part1.GND, FlAME_SENSOR.pin2, LM393.GND, part.1
  N2: NODEMCU.D1, part.4
  N3: NODEMCU.D2, part.5
  N4: NODEMCU.D4, FlAME_SENSOR.pin4
  N5: NODEMCU.D5, BUZZER.pin1
  N6: NODEMCU.D8, part.2
  N7: NODEMCU.A0, LM393.AO

notes:
  Ranganathaswamy Y S
  DHT11
  5v
  3.3v
  gnd
  OUTPUTS
  A0
  +
  -
  S

custom parts:
  KY-015 Temperature & Humidity Sensor Module: KY-015 temperature and humidity sensor module, provides a low-latency serial interface to measure humidity and temperature.
  NodeMCU V1.0: ESP8266 based NodeMCU
  KY-026: ky-026 flame sensor module
  FC-28 Soil Hygrometer Module: The FC-28 is a soil hygrometer module that uses the Texas Instruments LM393 comparator chip to provide an analog measurement of soil humidity. The digital output is high when soil moisture is over a certain threshold, as determined by adjusting the potentiometer.

// code stored in the sketch: Project_G.ino
#define CAYENNE_DEBUG
#define CAYENNE_PRINT Serial
#include <CayenneMQTTESP8266.h>
#include "DHT.h"
#define DHTTYPE DHT11
#define DHTPIN D3
#define valve1 D1
#define valve2 D2
#define flamePin D4
#define buzzer D5
#define moisturePin A0

char ssid[] = "Keerthi";
char wifiPassword[] = "12345678";

 
char username[] = "f6895170-c916-11eb-a2e4-b32ea624e442";
char password[] = "5461705d5593d7c76fb3ca09349df28091897ab7";
char clientID[] = "5bef1b80-c9c1-11eb-883c-638d8ce4c23d";

unsigned long lastMillis = 0;
int motor=D8;
int Flame=HIGH;
float moisturePercentage;
DHT dht(DHTPIN, DHTTYPE);
int FlameValue=0;


void setup() {
	Serial.begin(9600);
	Cayenne.begin(username, password, clientID, ssid, wifiPassword);
  dht.begin();
  pinMode(flamePin,INPUT);
  pinMode(motor,OUTPUT);
  pinMode(valve1,OUTPUT);
  pinMode(valve2,OUTPUT);
  pinMode(buzzer,OUTPUT);

  digitalWrite(motor,LOW);
  
}

void loop() {
	Cayenne.loop();
   float h = dht.readHumidity();
   float t = dht.readTemperature();
   moisturePercentage = ( 100.00 - ( (analogRead(moisturePin) / 1023.00) * 100.00 ));
   Flame=digitalRead(flamePin);
   if(Flame==HIGH){
    FlameValue=5;//random value for mapping high
    digitalWrite(buzzer,HIGH);
   }
   else if (Flame==LOW){
    FlameValue=8;
    digitalWrite(buzzer,LOW);}  // random value for low
   Cayenne.celsiusWrite(1, t);
   Cayenne.virtualWrite(2,h,TYPE_RELATIVE_HUMIDITY,UNIT_PERCENT);
   Cayenne.virtualWrite(3,moisturePercentage);
   Cayenne.virtualWrite(6,FlameValue);
   
  
}
CAYENNE_IN(0){

digitalWrite(motor,!getValue.asInt());
}

CAYENNE_IN(4){

digitalWrite(valve1,!getValue.asInt());
}

CAYENNE_IN(5){

digitalWrite(valve2,!getValue.asInt());
}

/*CAYENNE_IN(7){

digitalWrite(buzzer,!getValue.asInt());
}*/
